// Logisim project 2nd.circ as structural Verilog: 1 circuit, main circuit main
module main (
  input  C,
  input  B,
  input  A,
  input  C_2,
  input  B_2,
  input  A_2,
  input  D,
  input  C_3,
  input  B_3,
  input  A_3,
  input  A_4,
  input  B_4,
  input  C_4,
  input  D_2,
  input  C_5,
  input  B_5,
  input  A_5,
  output out_18,
  output out_19,
  output out_20,
  output out_21,
  output out_22
);

  wire A_C_out, A_nBC_out, AB_nD_out, AB_out, AC_2_out, AC_out, and_3_out, and_4_out, B_A_C_out, B_C_out,
       B_nD_out, BC_B_C_out, BC_out, nA_out, nAB_out, nAC_2_out, nAC_out, nB_out, nBC_out, nCD_out, nD_out,
       not_1_out, not_2_out, not_3_out, not_4_out, or_1_out, or_2_out, or_4_out, or_5_out;

  not nD (nD_out, D_2);
  not not_1 (not_1_out, C_3);
  not not_2 (not_2_out, A_4);
  or B_C (B_C_out, B, C);
  and BC (BC_out, B, C);
  and nCD (nCD_out, not_1_out, D);
  not nB (nB_out, B_5);
  and AB (AB_out, A, B);
  and AC (AC_out, A_2, C_2);
  or A_C (A_C_out, A_2, C_2);
  and nAC (nAC_out, not_2_out, C_4);
  and nAB (nAB_out, not_2_out, B_4);
  and BC_B_C (BC_B_C_out, B_C_out, BC_out);
  not not_3 (not_3_out, B_3);
  not nA (nA_out, A_5);
  and B_A_C (B_A_C_out, B_2, A_C_out);
  and nBC (nBC_out, not_3_out, C_3);
  or or_1 (or_1_out, nAC_out, C_4);
  or or_2 (or_2_out, nAB_out, C_4);
  and and_1 (out_18, AB_out, BC_B_C_out);
  or or_3 (out_19, A_2, AC_out, B_A_C_out);
  or or_4 (or_4_out, nBC_out, nCD_out);
  and and_2 (out_21, or_1_out, or_2_out);
  and nAC_2 (nAC_2_out, C_5, nA_out);
  and B_nD (B_nD_out, B_5, nD_out);
  and A_nBC (A_nBC_out, A_5, nB_out, C_5);
  and AB_nD (AB_nD_out, A_5, B_5, nD_out);
  not not_4 (not_4_out, A_3);
  and AC_2 (AC_2_out, A_5, C_5);
  and and_3 (and_3_out, B_3, or_4_out);
  or or_5 (or_5_out, B_5, AC_2_out);
  or or_6 (out_20, not_4_out, and_3_out);
  and and_4 (and_4_out, or_5_out, nAC_2_out);
  or or_7 (out_22, and_4_out, B_nD_out, A_nBC_out, AB_nD_out, B_5);

  // Notes on the sheet:
  //   !st EXAMPLE
  //   2nd EXAMPLE
  //   4th Example
  //   5th Example
  //   3rd EXAMPLE
  //   ~AB+C
  //   ~AC+B
  //   AB + BC(B+C)
  //   A+AC+B(A+C)
  //   ~BC+~CD
  //   (~AC+B)(~AB+C)
  //   B(~BC+~CD)
  //   AC+B
  //   ~AC(AC+B)
endmodule
